// Logisim project task2.circ as structural Verilog: 3 circuits, main circuit main
module main (
  input  in_1
);

  wire bcd_to_7_segment_decoder_2_p1, bcd_to_7_segment_decoder_3_p1, binary_to_bcd_converter_1_p2, clock,
       comparator_1_eq, comparator_2_eq, comparator_3_eq, comparator_4_eq, comparator_5_eq, j_k_ff_1_q,
       j_k_ff_2_q;
  wire [7:0] counter_1_q;

  Clock clock_1 (.out(clock));
  Counter #(.max('hf)) counter_1 (.clr(in_1), .clk(clock), .Q(counter_1_q));  // open: load, up, count, D, carry
  // BCD_to_7_Segment_decoder bcd_to_7_segment_decoder_1: pin names not known
  // BCD_to_7_Segment_decoder bcd_to_7_segment_decoder_2: pin names not known; wires that end beside it: bcd_to_7_segment_decoder_2_p1
  _7_Segment_Display u_7_segment_display_1 ();  // open: g, f, a, b, e, d, c, dp
  _7_Segment_Display u_7_segment_display_2 ();  // open: g, f, a, b, e, d, c, dp
  // Binary_to_BCD_converter #(.binvalue(8)) binary_to_bcd_converter_1: pin names not known; wires that end beside it: counter_1_q, binary_to_bcd_converter_1_p2, binary_to_bcd_converter_1_p2, bcd_to_7_segment_decoder_2_p1
  Comparator comparator_1 (.a({8{1'b0}}), .b(counter_1_q), .eq(comparator_1_eq));  // open: gt, lt
  Comparator comparator_2 (.a(8'h2), .b(counter_1_q), .eq(comparator_2_eq));  // open: gt, lt
  Comparator comparator_3 (.a(8'ha), .b(counter_1_q), .eq(comparator_3_eq));  // open: gt, lt
  Comparator comparator_4 (.a(8'h5), .b(counter_1_q), .eq(comparator_4_eq));  // open: gt, lt
  Comparator comparator_5 (.a(8'ha), .b(counter_1_q), .eq(comparator_5_eq));  // open: gt, lt
  // BCD_to_7_Segment_decoder bcd_to_7_segment_decoder_3: pin names not known; wires that end beside it: bcd_to_7_segment_decoder_3_p1, bcd_to_7_segment_decoder_3_p1
  _7_Segment_Display u_7_segment_display_3 ();  // open: g, f, a, b, e, d, c, dp
  LED led_1 (.in(comparator_1_eq));
  J_K_Flip_Flop j_k_ff_1 (
    .J(comparator_2_eq), .K(comparator_3_eq), .clk(clock), .Q(j_k_ff_1_q));  // open: Qn, preset, reset
  J_K_Flip_Flop j_k_ff_2 (
    .J(comparator_4_eq), .K(comparator_5_eq), .clk(clock), .Q(j_k_ff_2_q));  // open: Qn, preset, reset
  // Buzzer buzzer_1: pin names not known; wires that end beside it: 14'h52f, comparator_1_eq
  // Buzzer buzzer_2: pin names not known; wires that end beside it: 14'h320, j_k_ff_1_q
  // Buzzer buzzer_3: pin names not known; wires that end beside it: 14'h42a, j_k_ff_2_q
  // Digital_Oscilloscope digital_oscilloscope_1: pin names not known; wires that end beside it: clock, comparator_1_eq, j_k_ff_1_q, j_k_ff_2_q
endmodule

module add_by_ram (
  input  [7:0] in_1,
  input  [7:0] in_2,
  output [7:0] out_3
);

  // Probe on in_1
  // Probe on in_2
  Adder adder_1 (.a(in_1), .b(in_2), .out(out_3));  // open: cin, cout
  // Probe on out_3
endmodule

module tut_circut (
  input  in_1
);

  wire clock_1_out;
  wire [7:0] counter_1_q, ram_1_dout, ram_2_dout;

  Clock clock_1 (.out(clock_1_out));
  Counter counter_1 (.Q(counter_1_q), .clk(clock_1_out));  // open: load, D, count, carry, up, clr
  RAM ram_1 (.addr(counter_1_q), .oe(in_1), .clk(clock_1_out), .dout(ram_1_dout));  // open: we, din
  RAM ram_2 (.addr(counter_1_q), .oe(in_1), .clk(clock_1_out), .dout(ram_2_dout));  // open: we, din
  Register register_1 (.D(ram_1_dout), .en(in_1), .clk(clock_1_out));  // open: Q, clr
  Register register_2 (.D(ram_2_dout), .en(in_1), .clk(clock_1_out));  // open: Q, clr
endmodule
